# Fritzing sketch prototype_wiring (saved by Fritzing 0.9.1b)
circuit board: 8.46667cm x 5.64444cm

parts:
  Bauteil1 = Arduino Leonardo (Rev3b)
  LED1 = LED - 5mm [color="Red (633nm)" package="5 mm [THT]"]
  LED2 = LED - 5mm [color="Green (570nm)" package="5 mm [THT]"]
  R1 = Resistor [tolerance=±5% resistance=220 package=THT]
  J1 = Piezo Speaker
  S1 = Pushbutton [package="[THT]"]
  U1 = AUDIO-JACK2 [package=audio-jack-3.5mm-smd]

nets:
  N1: Bauteil1.D4/A6, LED1.anode
  N2: Bauteil1.D6_PWM/A7, J1.pin2, U1.RING
  N3: Bauteil1.D7, LED2.anode
  N4: Bauteil1.5V, S1.Pin_3, S1.Pin_4
  N5: Bauteil1.GND, LED1.cathode, LED2.cathode, R1.Pin_0, J1.pin1, U1.TSH
  N6: Bauteil1.A5, R1.Pin_1, S1.Pin_1, S1.Pin_2
